# Fritzing sketch leds_PCB (saved by Fritzing 0.8.5b)
circuit board: 2.23886cm x 6.17375cm
stripboards: 1

parts:
  Pad1 = Pad [width=0.821022929292932 height=0.8723104040404 connect=center]
  Pad3 = Pad [width=0.821022929292932 height=0.8723104040404 connect=center]
  Pad4 = Pad [width=0.821022929292932 height=0.8723104040404 connect=center]
  Pad5 = Pad [width=0.821022929292932 height=0.8723104040404 connect=center]
  Pad6 = Pad [width=0.821022929292932 height=0.8723104040404 connect=center]
  Pad7 = Pad [width=0.821022929292932 height=0.8723104040404 connect=center]
  Pad14 = Pad [width=0.821022929292932 height=0.8723104040404 connect=center]
  Pad15 = Pad [width=0.821022929292932 height=0.8723104040404 connect=center]
  Pad16 = Pad [width=0.821022929292932 height=0.8723104040404 connect=center]
  Pad17 = Pad [width=0.821022929292932 height=0.8723104040404 connect=center]
  Pad18 = Pad [width=0.821022929292932 height=0.8723104040404 connect=center]
  Pad19 = Pad [width=0.821022929292932 height=0.8723104040404 connect=center]
  Pad20 = Pad [width=0.821022929292932 height=0.8723104040404 connect=center]
  Pad21 = Pad [width=0.821022929292932 height=0.8723104040404 connect=center]
  Pad22 = Pad [width=0.821022929292932 height=0.8723104040404 connect=center]
  Pad23 = Pad [width=0.821022929292932 height=0.8723104040404 connect=center]
  Pad24 = Pad [width=0.821022929292932 height=0.8723104040404 connect=center]
  Pad25 = Pad [width=0.821022929292932 height=0.8723104040404 connect=center]
  Pad26 = Pad [width=0.821022929292932 height=0.8723104040404 connect=center]
  Pad27 = Pad [width=0.821022929292932 height=0.8723104040404 connect=center]
  Pad28 = Pad [width=0.821022929292932 height=0.8723104040404 connect=center]
  Pad29 = Pad [width=0.821022929292932 height=0.8723104040404 connect=center]
  Pad30 = Pad [width=0.821022929292932 height=0.8723104040404 connect=center]
  Pad31 = Pad [width=0.821022929292932 height=0.8723104040404 connect=center]
  ISP9 = male pin header, 8 pins [form="♂ (male)"]
  ISP6 = male pin header, 8 pins [form="♂ (male)"]
  ISP10 = male pin header, 8 pins [form="♂ (male)"]
  ISP7 = male pin header, 8 pins [form="♂ (male)"]

nets:
  N1: Pad1.pad, Pad24.pad, ISP6.pin3, ISP6.pin6, ISP7.pin3, ISP7.pin6
  N2: Pad3.pad, Pad5.pad, Pad6.pad
  N3: Pad4.pad, Pad22.pad, ISP6.pin4, ISP6.pin5, ISP7.pin4, ISP7.pin5
  N4: Pad7.pad, Pad21.pad, ISP6.pin2, ISP6.pin7, ISP7.pin2, ISP7.pin7
  N5: Pad14.pad, Pad17.pad, Pad19.pad
  N6: Pad15.pad, Pad28.pad, ISP9.pin2, ISP9.pin7, ISP10.pin2, ISP10.pin7
  N7: Pad16.pad, Pad27.pad, ISP9.pin4, ISP9.pin5, ISP10.pin4, ISP10.pin5
  N8: Pad18.pad, Pad30.pad, ISP9.pin3, ISP9.pin6, ISP10.pin3, ISP10.pin6
  N9: Pad20.pad, Pad23.pad, Pad25.pad
  N10: Pad26.pad, Pad29.pad, Pad31.pad
  N11: ISP9.pin1, ISP9.pin8, ISP6.pin1, ISP6.pin8, ISP10.pin1, ISP10.pin8, ISP7.pin1, ISP7.pin8

notes:
  +12
  G
  R
  B
  GND2
  v1.5
  GND1
