# Fritzing sketch semaforo_ruido_MainPCB (saved by Fritzing 0.8.5b)
circuit board: 9.8cm x 6.00104cm
breadboards: 1

parts:
  ATMEGA328P-PU = atmega328 [package=dip]
  R5 = Resistor [tolerance=±5% resistance=1k part_number=1k package=THT]
  R4 = Resistor [tolerance=±5% resistance=1k part_number=1k package=THT]
  R3 = Resistor [tolerance=±5% resistance=1k part_number=1k package=THT]
  R2 = Resistor [tolerance=±5% resistance=1k part_number=1k package=THT]
  Power_plug1 = Power plug
  R1 = Resistor [tolerance=±5% resistance=330 part_number=330 package=THT]
  LM7805 = Voltage Regulator - 5V [package="TO220 [THT]"]
  C1 = Ceramic Capacitor [capacitance=22pF part_number=22pF package="200 mil [THT, multilayer]"]
  C2 = Ceramic Capacitor [capacitance=22pF part_number=22pF package="200 mil [THT, multilayer]"]
  XTAL1 = Crystal [frequency="16 Mhz" part_number=16Mhz package=THT]
  R6 = Resistor [tolerance=±5% resistance=10k power=250mW part_number=10k package=THT]
  R8 = Resistor [tolerance=±5% resistance=10k power=250mW part_number=10k package=THT]
  R9 = Resistor [tolerance=±5% resistance=10k power=250mW part_number=10k package=THT]
  LED1 = LED - 5mm [color="Green (565nm)" package="5 mm [THT]"]
  R10 = Rotary Potentiometer (Large) [maximum_resistance=10kΩ part_number=10k package=THT]
  R11 = Rotary Potentiometer (Large) [maximum_resistance=10kΩ part_number=10k package=THT]
  R12 = Rotary Potentiometer (Large) [maximum_resistance=10kΩ part_number=10k package=THT]
  R7 = Resistor [tolerance=±5% resistance=10k power=250mW part_number=10k package=THT]
  Pad1 = Pad [width=2.25777777777779 height=2.74158730158731 connect=center]
  S1 = Pushbutton [package="[THT]"]
  Mic0 = male pin header, 3 pins [form="♂ (male)"]
  J8 = male pin header, 3 pins [form="♂ (male)"]
  J9 = male pin header, 3 pins [form="♂ (male)"]
  Mic1 = male pin header, 3 pins [form="♂ (male)"]
  J7 = male pin header, 6 pins [form="♂ (male)"]
  J5 = female pin header, 6 pins [form="♀ (female)"]
  J6 = female pin header, 6 pins [form="♀ (female)"]
  J3 = female pin header, 8 pins [form="♀ (female)"]
  J4 = female pin header, 8 pins [form="♀ (female)"]
  C4 = Electrolytic Capacitor [capacitance=10µF package="100 mil [THT, electrolytic]"]
  Q1 = NPN-Transistor [part_number=2222A package="TO92 [THT]"]
  C3 = Electrolytic Capacitor [capacitance=10µF package="100 mil [THT, electrolytic]"]
  Q2 = NPN-Transistor [part_number=2222A package="TO92 [THT]"]
  Q3 = NPN-Transistor [part_number=2222A package="TO92 [THT]"]
  Q4 = NPN-Transistor [part_number=2222A package="TO92 [THT]"]
  J1 = male pin header, 2 pins [form="♂ (male)"]
  J2 = screw terminal, 5 pins

nets:
  RESET: ATMEGA328P-PU.RESET, R6.Pin_0, S1.Pin_1, S1.Pin_2, J7.pin6, J6.pin6
  D0(RX): ATMEGA328P-PU.D0_(RX), J7.pin4, J3.pin1
  D1(TX): ATMEGA328P-PU.D1_(TX), J7.pin5, J3.pin2
  D2: ATMEGA328P-PU.D2, J3.pin3
  D3(PWM): ATMEGA328P-PU.D3_(PWM), J3.pin4
  D4: ATMEGA328P-PU.D4, R4.Pin_1, J3.pin5
  +5V: ATMEGA328P-PU.VCC, ATMEGA328P-PU.AVCC, ATMEGA328P-PU.AREF, LM7805.output_voltage, R6.Pin_1, LED1.anode, R10.leg1, R11.leg1, R12.leg1, Mic0.pin3, J8.pin3, J9.pin3, Mic1.pin3, J7.pin3, J6.pin4, J4.pin8, C4.+
  GND: ATMEGA328P-PU.GND, Power_plug1.GND, R1.Pin_0, LM7805.GND, C1.0, C2.0, R8.Pin_0, R9.Pin_0, R10.leg2, R11.leg2, R12.leg2, R7.Pin_1, Pad1.pad, S1.Pin_3, S1.Pin_4, Mic0.pin2, J8.pin2, J9.pin2, Mic1.pin2, J7.pin1, J6.pin2, J6.pin3, J4.pin7, C4.-, Q1.E, C3.-, Q2.E, Q3.E, Q4.E
  XLAT1: ATMEGA328P-PU.XLAT1, C2.1, XTAL1.pin_0
  XLAT2: ATMEGA328P-PU.XLAT2, C1.1, XTAL1.pin_1
  D5(PWM): ATMEGA328P-PU.D5_(PWM), R3.Pin_1, J3.pin6
  D6(PWM): ATMEGA328P-PU.D6_(PWM), J3.pin7
  D7: ATMEGA328P-PU.D7, J3.pin8
  D8: ATMEGA328P-PU.D8, J4.pin1
  D9 (PWM): ATMEGA328P-PU.D9_(PWM), J4.pin2
  D10 (PWM): ATMEGA328P-PU.D10_(PWM), R2.Pin_1, J4.pin3
  D11 (PWM): ATMEGA328P-PU.D11_(PWM), J4.pin4
  D12: ATMEGA328P-PU.D12, J4.pin5
  D13: ATMEGA328P-PU.D13, J4.pin6
  A0: ATMEGA328P-PU.A0, R8.Pin_1, Mic0.pin1, J8.pin1, J5.pin6
  A1: ATMEGA328P-PU.A1, R9.Pin_1, J9.pin1, Mic1.pin1, J5.pin5
  A2: ATMEGA328P-PU.A2, R10.wiper, J5.pin4
  A3: ATMEGA328P-PU.A3, R11.wiper, J5.pin3
  A4: ATMEGA328P-PU.A4, R12.wiper, J5.pin2
  A5: ATMEGA328P-PU.A5, R5.Pin_1, J5.pin1
  N1: R5.Pin_0, Q1.B
  N2: R4.Pin_0, Q2.B
  N3: R3.Pin_0, Q3.B
  N4: R2.Pin_0, Q4.B
  N5: Power_plug1.VCC, J1.pin2
  N6: R1.Pin_1, LED1.cathode
  +12V: LM7805.input_voltage, J6.pin1, C3.+, J1.pin1, J2.pin5
  N7: R7.Pin_0, J7.pin2
  N8: Q1.C, J2.pin1
  N9: Q2.C, J2.pin2
  N10: Q3.C, J2.pin3
  N11: Q4.C, J2.pin4

notes:
  By Korama.es
  08/01/2014
  v1.5
  +12V
  CC-BY-SA-3.0 ES
  5V
  12V
  Mic 1
  del Ruido
  "OpenSource"
  Semaforo
  EQComponentes.com
  PCB-Fab by
  Mic 0
  Semaforo del Ruido OpenSource, by Korama.es  - http://semafororuido.korama.es Licenciado bajo Creative Commons - BY - SA 3.0 ES, v1.5
