# Fritzing sketch wired_sensor_PCB (saved by Fritzing 0.8.5b)
circuit board: 3.5cm x 3.6cm
breadboards: 1

parts:
  LM358 = LM 358 Dual Op-Amp [part_number=LM358 package="DIP8 [THT]"]
  R5 = Resistor [tolerance=±5% resistance=1k part_number=1kΩ power=250mW package=THT]
  R4 = Resistor [tolerance=±5% resistance=10k power=250mW part_number=10K package=THT]
  C5 = Ceramic Capacitor [capacitance=0.1µF part_number=0.1uF package="200 mil [THT, multilayer]"]
  R7 = Resistor [tolerance=±5% resistance=10k part_number=10K power=250mW package=THT]
  R3 = Resistor [tolerance=±5% resistance=10k part_number=10K power=250mW package=THT]
  R6 = Resistor [tolerance=±5% resistance=10k part_number=10K power=250mW package=THT]
  C1 = Ceramic Capacitor [capacitance=0.1µF part_number=0.1uF package="200 mil [THT, multilayer]"]
  R1 = Resistor [tolerance=±5% resistance=1k part_number=1kΩ power=250mW package=THT]
  R2 = Resistor [tolerance=±5% resistance=10k part_number=10K power=250mW package=THT]
  C3 = Electrolytic Capacitor [capacitance=4.7µF part_number=4.7uF package="100 mil [THT, electrolytic]"]
  C4 = Ceramic Capacitor [capacitance=0.1µF part_number=0.1uF package="200 mil [THT, multilayer]"]
  MIC1 = Microphone
  C2 = Electrolytic Capacitor [capacitance=4.7µF part_number=4.7uF package="100 mil [THT, electrolytic]"]
  R8 = Trimmer Potentiometer [maximum_resistance=5kΩ part_number=5kΩ package=THT]
  J1 = female pin header, 3 pins [form="♀ (female)"]

nets:
  N1: LM358.connector0, R4.Pin_0, C1.0
  N2: LM358.connector1, R5.Pin_0, R4.Pin_1
  N3: LM358.connector2, LM358.connector4, R3.Pin_1, R6.Pin_0
  GND: LM358.connector3, R3.Pin_0, C3.-, C4.0, MIC1.pin1, R8.leg2, J1.pin2
  N4: LM358.connector5, R1.Pin_0, R2.Pin_0
  N5: LM358.connector6, R2.Pin_1, C2.+
  +5V: LM358.connector7, R7.Pin_1, R6.Pin_1, C3.+, C4.1, J1.pin3
  N6: R5.Pin_1, C5.1
  N7: C5.0, R7.Pin_0, MIC1.pin2
  N8: C1.1, R1.Pin_1
  N9: C2.-, R8.leg1
  A0: R8.wiper, J1.pin1

notes:
  08/01/2014
  CC-BY-SA-3.0 ES
  By Korama.es
  Sensor Sonido Wireless, by Korama.es  - http://semafororuido.korama.es Licenciado bajo Creative Commons - BY - SA 3.0 ES, v1.4
  v1.5
