# Fritzing sketch Esquema Semaforo Ruido (saved by Fritzing 0.7.11b)
perfboards: 1

parts:
  Parte1 = Arduino MP3 Player Shield  # not connected
  K1 = Relay [part_number="Rele 10A 1C 6V" package=THT]
  220V_INPUT = Screw terminal - 2 pins [package=THT]
  220V_#1 = Screw terminal - 2 pins [package=THT]
  220V_#2 = Screw terminal - 2 pins [package=THT]
  J0 = female pin header, 2 pins [form="♀ (female)"]
  K2 = Relay [part_number="Rele 10A 1C 6V" package=THT]
  D2 = Rectifier Diode [part_number=1N4007 package="300 mil [THT]"]
  K3 = Relay [part_number="Rele 10A 1C 6V" package=THT]
  220V_#3 = Screw terminal - 2 pins [package=THT]
  D3 = Rectifier Diode [part_number=1N4007 package="300 mil [THT]"]
  K4 = Relay [part_number="Rele 10A 1C 6V" package=THT]
  220V_#4 = Screw terminal - 2 pins [package=THT]
  D4 = Rectifier Diode [part_number=1N4007 package="300 mil [THT]"]
  R4 = Resistor [tolerance=±5% resistance=1k package=THT]
  Arduino1 = Arduino
  Parte2 = Breakout Board for Electret Microphone
  Rp1 = Rotary Potentiometer (Large) [maximum_resistance=10kΩ part_number=10kΩ package=THT]
  Rp2 = Rotary Potentiometer (Large) [maximum_resistance=10kΩ part_number=10kΩ package=THT]
  Rp3 = Rotary Potentiometer (Large) [maximum_resistance=10kΩ part_number=10kΩ package=THT]
  Q4 = NPN-Transistor [part_number=" 2.N.3904" package="TO92 [THT]"]
  Q3 = NPN-Transistor [part_number=" 2.N.3904" package="TO92 [THT]"]
  R2 = Resistor [tolerance=±5% resistance=1k package=THT]
  R3 = Resistor [tolerance=±5% resistance=1k package=THT]
  D1 = Rectifier Diode [part_number=1N4007 package="300 mil [THT]"]
  Q1 = NPN-Transistor [part_number=" 2.N.3904" package="TO92 [THT]"]
  Q2 = NPN-Transistor [part_number=" 2.N.3904" package="TO92 [THT]"]
  R1 = Resistor [tolerance=±5% resistance=1k package=THT]

nets:
  5V: K1.COIL1, J0.pin2, K2.COIL1, D2.cathode, K3.COIL1, D3.cathode, K4.COIL1, D4.cathode, Arduino1.+5V, Parte2.VCC, Rp1.leg1, Rp2.leg1, Rp3.leg1, D1.cathode
  N1: K1.C1, K1.C2, 220V_INPUT.pin1, K2.C1, K2.C2, K3.C1, K3.C2, K4.C1, K4.C2
  N2: K1.COIL2, D1.anode, Q1.C
  N3: K1.B, 220V_#1.pin2
  N4: 220V_INPUT.pin2, 220V_#1.pin1, 220V_#2.pin1, 220V_#3.pin1, 220V_#4.pin1
  N5: 220V_#2.pin2, K2.B
  GND: J0.pin1, Arduino1.GND, Parte2.GND, Rp1.leg2, Rp2.leg2, Rp3.leg2, Q4.E, Q3.E, Q1.E, Q2.E
  N6: K2.COIL2, D2.anode, Q2.C
  N7: K3.COIL2, D3.anode, Q3.C
  N8: K3.B, 220V_#3.pin2
  N9: K4.COIL2, D4.anode, Q4.C
  N10: K4.B, 220V_#4.pin2
  N11: R4.Pin_0, Q4.B
  N12: R4.Pin_1, Arduino1.D5
  N13: Arduino1.D3, R1.Pin_1
  N14: Arduino1.A0, Rp1.wiper
  N15: Arduino1.A1, Rp2.wiper
  N16: Arduino1.A2, Rp3.wiper
  N17: Arduino1.A3, Parte2.AUD
  N18: Arduino1.A4, R3.Pin_1
  N19: Arduino1.A5, R2.Pin_1
  N20: Q3.B, R3.Pin_0
  N21: R2.Pin_0, Q2.B
  N22: Q1.B, R1.Pin_0

notes:
  LUZ #1 - 220V
  +5V
  GND
  LUZ #2 - 220V
  LUZ #3 - 220V
  LUZ #4 - 220V
  ENTRADA: 220V
  Semaforo Ruido, Esquema General de Circuito, v.0.74
  Author: Lluis Toyos
  Email: info@korama.es
  Licence: GNU/GPL v3
  VOLUMEN MP3
  Umbral MIN
  Umbral MAX
  Este esquema esta licenciado bajo GNU/GPL v.3 , cuyo texto completo se encuentra en el archivo LICENSE.txt
  Volumen
